# Fritzing sketch HomeKit Light Switch (saved by Fritzing 0.9.3b)
breadboards: 1

parts:
  Onderdeel1 = FTDI Basic Programmer
  U1 = ESP8266 WiFi Module [part_number=ESP8266]
  S1 = Pushbutton [package="[THT]"]
  S2 = Pushbutton [package="[THT]"]
  S3 = Pushbutton [package="[THT]"]
  R2 = Resistor [tolerance=±5% resistance=10k package=THT]
  R3 = Resistor [tolerance=±5% resistance=10k package=THT]
  C1 = Electrolytic Capacitor [capacitance=1µF package="100 mil [THT, electrolytic]"]
  R4 = Resistor [tolerance=±5% resistance=10k package=THT]
  C2 = Capacitor [package=cap-pth-small2]

nets:
  N1: Onderdeel1.RXI, U1.TXD
  N2: Onderdeel1.TXO, U1.RXD
  N3: Onderdeel1.POWER, U1.VCC, R2.Pin_1, R3.Pin_1, C1.+, R4.Pin_1
  GND: Onderdeel1.GND, U1.GND, S1.Pin_3, S1.Pin_4, S2.Pin_3, S2.Pin_4, S3.Pin_3, S3.Pin_4, C1.-, C2.2
  N4: U1.GPIO_0, S2.Pin_1, S2.Pin_2, R2.Pin_0
  N5: U1.RST, S3.Pin_1, S3.Pin_2, R3.Pin_0
  N6: U1.GPIO_2, S1.Pin_1, S1.Pin_2, C2.1
  N7: U1.CH_PD, R4.Pin_0

notes:
  470μF ~ 6,3V
  PROGRAM
  RESET
  SWITCH
  www.StudioPieters.nl

custom parts:
  FTDI Basic Programmer: Description: This is the newest revision of our FTDI Basic. We now use a SMD 6-pin header on the bottom, which makes it smaller and more compact. Functionality has remained the same. This is a basic breakout board for the FTDI FT232RL USB to serial IC. The pinout of this board matches the FTDI cable to work with official Arduino and cloned 3.3V Arduino boards. It can also be used for general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
  ESP8266 WiFi Module: Generic WiFi Module based on the ESP8266 with onboard PCB antenna and UART communications
